// Logisim project generated_circuit.circ as structural Verilog: 1 circuit, main circuit sos
module sos (
  input  A,
  input  B,
  input  C,
  input  D,
  input  E,
  output OUT
);

  wire and_1_out, and_2_out, and_3_out, and_4_out, and_5_out, and_6_out, not_1_out, not_2_out, not_3_out,
       not_4_out, not_5_out, not_6_out, not_7_out, not_8_out, not_9_out, not_10_out, not_11_out, not_12_out,
       not_13_out, not_14_out;

  not not_1 (not_1_out, B);
  not not_2 (not_2_out, C);
  not not_3 (not_3_out, D);
  not not_4 (not_4_out, B);
  not not_5 (not_5_out, E);
  not not_6 (not_6_out, A);
  not not_7 (not_7_out, D);
  and and_1 (and_1_out, not_6_out, not_7_out, not_8_out);
  not not_8 (not_8_out, E);
  not not_9 (not_9_out, C);
  and and_2 (and_2_out, not_9_out, not_10_out);
  not not_10 (not_10_out, E);
  not not_11 (not_11_out, A);
  and and_3 (and_3_out, not_11_out, B, not_12_out);
  not not_12 (not_12_out, D);
  not not_13 (not_13_out, A);
  and and_4 (and_4_out, not_13_out, B, not_14_out);
  not not_14 (not_14_out, E);
  and and_5 (and_5_out, A, not_1_out, not_2_out, not_3_out);
  and and_6 (and_6_out, A, not_4_out, D, not_5_out);
  or or_1 (OUT, and_1_out, and_2_out, and_3_out, and_4_out, and_5_out, and_6_out);
endmodule
