// Logisim project simplified_circuit.circ as structural Verilog: 1 circuit, main circuit sos
module sos (
  output OUT
);

  wire A___16T_out, and_1_out, and_2_out, and_3_out, and_4_out, and_5_out, and_6_out, B___8T_out, C___4T_out,
       D___2T_out, E___T_out, not_1_out, not_2_out, not_3_out, not_4_out, not_5_out, or_1_out;

  Clock #(.highDuration(16), .lowDuration(16)) A___16T (.out(A___16T_out));
  Clock #(.highDuration(8), .lowDuration(8)) B___8T (.out(B___8T_out));
  Clock #(.highDuration(4), .lowDuration(4)) C___4T (.out(C___4T_out));
  Clock #(.highDuration(2), .lowDuration(2)) D___2T (.out(D___2T_out));
  Clock E___T (.out(E___T_out));
  not not_1 (not_1_out, A___16T_out);
  not not_2 (not_2_out, B___8T_out);
  not not_3 (not_3_out, C___4T_out);
  not not_4 (not_4_out, D___2T_out);
  not not_5 (not_5_out, E___T_out);
  and and_1 (and_1_out, not_1_out, not_4_out, not_5_out, not_5_out);
  and and_2 (and_2_out, not_3_out, not_3_out, not_5_out, not_5_out);
  and and_3 (and_3_out, not_1_out, B___8T_out, not_4_out, not_4_out);
  and and_4 (and_4_out, not_1_out, B___8T_out, not_5_out, not_5_out);
  and and_5 (and_5_out, A___16T_out, not_2_out, not_3_out, not_4_out);
  and and_6 (and_6_out, A___16T_out, not_2_out, D___2T_out, not_5_out);
  or or_1 (or_1_out, and_4_out, and_5_out, and_6_out, and_6_out);
  or or_2 (OUT, and_1_out, and_2_out, and_3_out, or_1_out);
endmodule
